# Fritzing sketch analog1 (saved by Fritzing 0.9.2b)
breadboards: 1

parts:
  Teensy_3_1 = Teensy 3.1
  Voltmeter1 = Voltmeter

nets:
  N1: Teensy_3_1.GND, Voltmeter1.Com
  N2: Teensy_3_1.A14/DAC, Voltmeter1.Positive

custom parts:
  Voltmeter: A Standard Multimeter in Current mode
