# Fritzing sketch pwm (saved by Fritzing 0.9.2b)
breadboards: 1

parts:
  Teensy_3_1 = Teensy 3.1
  Voltmeter1 = Voltmeter
  C1 = Ceramic Capacitor [capacitance=100nF package="100 mil [THT, multilayer]"]  # not connected

nets:
  N1: Teensy_3_1.GND, Voltmeter1.Com
  N2: Teensy_3_1.D9, Voltmeter1.Positive

custom parts:
  Voltmeter: A Standard Multimeter in Current mode
