# Fritzing sketch pwm3 (saved by Fritzing 0.9.2b)
breadboards: 1

parts:
  Teensy_3_1 = Teensy 3.1  # not connected
  LED1 = LED - 5mm [color="Red (633nm)" package="5 mm [THT]"]
  R1 = Resistor [tolerance=±5% resistance=220 package=THT]
  R2 = Trimmer Potentiometer [maximum_resistance=10kΩ package=THT]

nets:
  N1: LED1.anode, R1.Pin_1
  N2: R1.Pin_0, R2.leg1
